# Fritzing sketch LoRa Tx and Rx Test 1 (saved by Fritzing 0.9.3b)
breadboards: 2

parts:
  U2 = ESP32S-HiLetgo [part_number=ESP32S-HiLetgo]
  LED1 = LED - 3mm [color="Green (565nm)" package="3 mm [THT]"]
  R1 = Resistor [tolerance=±5% resistance=100 package=THT]
  Mod1 = RYLR896 [package=THT]
  U3 = ESP32S-HiLetgo [part_number=ESP32S-HiLetgo]
  LED2 = LED - 3mm [color="Orange (620nm)" package="3 mm [THT]"]
  R2 = Resistor [tolerance=±5% resistance=100 package=THT]
  Mod2 = RYLR896 [package=THT]

nets:
  N1: U2.3.3, Mod1.pin1
  N2: U2.GND, R1.Pin_0, Mod1.pin5
  N3: U2.GPIO2, LED1.cathode
  N4: U2.GPIO16, Mod1.pin3#3
  N5: U2.GPIO17, Mod1.pin3#2
  N6: LED1.anode, R1.Pin_1
  N7: U3.3.3, Mod2.pin1
  N8: U3.GND, R2.Pin_0, Mod2.pin5
  N9: U3.GPIO2, LED2.cathode
  N10: U3.GPIO16, Mod2.pin3#3
  N11: U3.GPIO17, Mod2.pin3#2
  N12: LED2.anode, R2.Pin_1

notes:
  TX
  RX

custom parts:
  ESP32S-HiLetgo: HiLetgo ESP-WROOM-32 ESP32 ESP-32S Development Board 2.4GHz Dual-Mode WiFi + Bluetooth Dual Cores Microcontroller The ESP32 integrated with Antenna switches, RF Balun, power amplifiers, low-noise amplifiers, filters, and management modules, and the entire solution occupies the least area of PCB. 2.4 GHz Wi-Fi plus Bluetooth dual-mode chip, with TSMC Ultra-low power consumption 40nm technology,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
  RYLR896: RYLR896 UART Interface 868/915mhz LORA Transceiver Module
