# Fritzing sketch Turbidity Sensor Circuit (saved by Fritzing 0.9.3b)
breadboards: 1

parts:
  U1 = ESP32S-HiLetgo [part_number=ESP32S-HiLetgo]
  Turbidity_Sensor_V1_1 = IC, DIP package, 6 pins [chip_label=IC]
  J1 = Infrared Proximity Sensor

nets:
  N1: U1.3.3, Turbidity_Sensor_V1_1.pin3
  N2: U1.GPIO34, Turbidity_Sensor_V1_1.pin2
  N3: U1.GND, Turbidity_Sensor_V1_1.pin1
  N4: Turbidity_Sensor_V1_1.pin4, J1.Vout
  N5: Turbidity_Sensor_V1_1.pin5, J1.Vcc
  N6: Turbidity_Sensor_V1_1.pin6, J1.GND

custom parts:
  ESP32S-HiLetgo: HiLetgo ESP-WROOM-32 ESP32 ESP-32S Development Board 2.4GHz Dual-Mode WiFi + Bluetooth Dual Cores Microcontroller The ESP32 integrated with Antenna switches, RF Balun, power amplifiers, low-noise amplifiers, filters, and management modules, and the entire solution occupies the least area of PCB. 2.4 GHz Wi-Fi plus Bluetooth dual-mode chip, with TSMC Ultra-low power consumption 40nm technology,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
